// Logisim project final_cpu_again.circ as structural Verilog: 4 circuits, main circuit main
module main (
  input  in_1
);

  wire Clear_RAM_out, clock_1_out, comparator_1_eq, comparator_2_eq, cpu_v0_circ_1_clk_out,
       cpu_v0_circ_1_write, double_clock_1_out_2, double_clock_2_out_2;
  wire [31:0] cpu_v0_circ_1_address_out, cpu_v0_circ_1_data_out, pull_resistor_1_node, pull_resistor_2_node,
       ram_1_dout;

  Clock clock_1 (.out(clock_1_out));
  Counter counter_1 (.clk(clock_1_out));  // open: load, D, count, Q, carry, up, clr
  DOUBLE_CLOCK double_clock_1 (.in_1(clock_1_out), .out_2(double_clock_1_out_2));
  CPU_v0_circ cpu_v0_circ_1 (
    .ENABLE_in(in_1), .CLK_in(clock_1_out), .DATA_in(ram_1_dout), .ADDRESS_out(cpu_v0_circ_1_address_out),
    .write(cpu_v0_circ_1_write), .CLK_out(cpu_v0_circ_1_clk_out), .DATA_out(cpu_v0_circ_1_data_out));  // open: INTERRUPT_in
  Pull_Resistor pull_resistor_1 (.node(pull_resistor_1_node));
  Pull_Resistor #(.pull(1)) pull_resistor_2 (.node(pull_resistor_2_node));
  Comparator #(.mode("unsigned"), .width(32)) comparator_1 (
    .a(cpu_v0_circ_1_address_out), .b(pull_resistor_1_node), .eq(comparator_1_eq));  // open: gt, lt
  Comparator #(.mode("unsigned"), .width(32)) comparator_2 (
    .a(cpu_v0_circ_1_address_out), .b(pull_resistor_2_node), .eq(comparator_2_eq));  // open: gt, lt
  DOUBLE_CLOCK double_clock_2 (.in_1(cpu_v0_circ_1_clk_out), .out_2(double_clock_2_out_2));
  Counter #(.max('hffffffff), .width(32)) counter_2 (
    .count(comparator_1_eq), .clk(double_clock_1_out_2));  // open: load, D, Q, carry, up, clr
  Counter #(.max('hffffffff), .width(32)) counter_3 (
    .count(comparator_2_eq), .clk(double_clock_1_out_2));  // open: load, D, Q, carry, up, clr
  Button Clear_RAM (.out(Clear_RAM_out));
  RAM #(.addrWidth(24), .clearpin("true"), .dataWidth(32), .enables("line"), .\type ("nonvolatile")) ram_1 (
    .addr(cpu_v0_circ_1_address_out[23:0]), .we(cpu_v0_circ_1_write), .clk(double_clock_2_out_2),
    .din(cpu_v0_circ_1_data_out), .dout(ram_1_dout), .clr(Clear_RAM_out));
  // also tied to GND on the sheet: {pull_resistor_1_node[0], pull_resistor_1_node[3], pull_resistor_1_node[5], pull_resistor_1_node[6], pull_resistor_1_node[7], pull_resistor_1_node[8], pull_resistor_1_node[9], pull_resistor_1_node[10], pull_resistor_1_node[11], pull_resistor_1_node[12], pull_resistor_1_node[13], pull_resistor_1_node[14], pull_resistor_1_node[15], pull_resistor_1_node[16], pull_resistor_1_node[17], pull_resistor_1_node[18], pull_resistor_1_node[19], pull_resistor_1_node[20], pull_resistor_1_node[21], pull_resistor_1_node[22], pull_resistor_1_node[23], pull_resistor_1_node[24], pull_resistor_1_node[25], pull_resistor_1_node[26], pull_resistor_1_node[27], pull_resistor_1_node[28], pull_resistor_1_node[29], pull_resistor_1_node[30], pull_resistor_1_node[31]}
  // also tied to VCC on the sheet: {pull_resistor_1_node[1], pull_resistor_1_node[2], pull_resistor_1_node[4]}
endmodule

module CPU_v0_circ (
  input  ENABLE_in,
  input  CLK_in,
  input  [31:0] DATA_in,
  input  INTERRUPT_in,
  output [31:0] ADDRESS_out,
  output write,
  output CLK_out,
  output [31:0] DATA_out
);

  wire alt_addr, alt_addr_sel, and_2_out, and_3_out, and_4_out, and_5_out, and_6_out, and_7_out, and_8_out,
       and_9_out, both_regs, clock_edge_enabler_1_clk_out, clock_edge_enabler_2_clk_out,
       clock_edge_enabler_3_clk_out, comparator_1_eq, data_out_sel, delay_falling, delay_rising,
       demultiplexer_2_out30, enable_falling_edge, F, increment_address, nor_1_out, nor_2_out, nor_3_out,
       PC_write, pull_resistor_1_node, pull_resistor_3_node, pull_resistor_36_node, pull_resistor_38_node,
       pull_resistor_39_node, pull_resistor_40_node, pull_resistor_41_node, pull_resistor_42_node,
       pull_resistor_43_node, pull_resistor_44_node, pull_resistor_45_node, pull_resistor_46_node,
       pull_resistor_47_node, pull_resistor_48_node, pull_resistor_49_node, pull_resistor_50_node,
       pull_resistor_51_node, pull_resistor_52_node, pull_resistor_53_node, pull_resistor_54_node,
       pull_resistor_55_node, pull_resistor_56_node, pull_resistor_57_node, pull_resistor_58_node,
       pull_resistor_59_node, pull_resistor_60_node, pull_resistor_61_node, pull_resistor_62_node,
       pull_resistor_63_node, pull_resistor_64_node, pull_resistor_65_node, pull_resistor_66_node, reg_write,
       select_temp_in, t_ff_1_q, t_ff_1_qn, write_IR, write_temp, X_addr, X_imm, Y_addr, Y_imm;
  wire [4:0] multiplexer_5_out, pull_resistor_4_node, undriven_2, X, Y;
  wire [31:0] address_alt_out, ALU_out, data_out_t, multiplexer_1_out, PC_in, PC_out, pull_resistor_5_node,
       pull_resistor_7_node, pull_resistor_8_node, pull_resistor_9_node, pull_resistor_10_node,
       pull_resistor_11_node, pull_resistor_12_node, pull_resistor_13_node, pull_resistor_14_node,
       pull_resistor_15_node, pull_resistor_16_node, pull_resistor_17_node, pull_resistor_18_node,
       pull_resistor_19_node, pull_resistor_20_node, pull_resistor_21_node, pull_resistor_22_node,
       pull_resistor_23_node, pull_resistor_24_node, pull_resistor_25_node, pull_resistor_26_node,
       pull_resistor_27_node, pull_resistor_28_node, pull_resistor_29_node, pull_resistor_30_node,
       pull_resistor_31_node, pull_resistor_32_node, pull_resistor_33_node, pull_resistor_34_node,
       reg_data_in, reg_data_out, reg_data_out_2, register_3_q, register_4_q, register_5_q, register_6_q,
       register_7_q, register_8_q, register_9_q, register_10_q, register_11_q, register_12_q, register_13_q,
       register_14_q, register_15_q, register_16_q, register_17_q, register_18_q, register_19_q,
       register_20_q, register_21_q, register_22_q, register_23_q, register_24_q, register_25_q,
       register_26_q, register_27_q, register_28_q, register_29_q, register_30_q, register_31_q, temp_reg,
       undriven;
  wire [31:11] register_2_q;

  Pull_Resistor #(.pull(1)) pull_resistor_1 (.node(pull_resistor_1_node));
  clock_edge_enabler clock_edge_enabler_1 (
    .CLK_in(CLK_out), .enable_rising_edge(delay_rising), .enable_falliong_edge(delay_falling),
    .CLK_out(clock_edge_enabler_1_clk_out));
  Comparator #(.mode("unsigned"), .width(5)) comparator_1 (.a(X), .b(Y), .eq(comparator_1_eq));  // open: gt, lt
  T_Flip_Flop t_ff_1 (
    .T(pull_resistor_1_node), .clk(clock_edge_enabler_1_clk_out), .Q(t_ff_1_q), .Qn(t_ff_1_qn));  // open: reset, preset
  buf and_1 (CLK_out, CLK_in);  // AND_Gate
  Pull_Resistor pull_resistor_2 (.node(DATA_in));
  nor nor_1 (nor_1_out, Y_imm, Y_addr);
  nor nor_2 (nor_2_out, X_addr, X_imm);
  and and_2 (and_2_out, ~register_2_q[15], ~register_2_q[14], ~register_2_q[13], ~register_2_q[12], register_2_q[11]);  // AND_Gate
  and and_3 (and_3_out, ~comparator_1_eq, and_2_out);  // AND_Gate
  Multiplexer #(.width(32)) multiplexer_1 (
    .in0(DATA_in), .in1(reg_data_out), .out(multiplexer_1_out), .sel(select_temp_in));
  and and_4 (and_4_out, F, and_3_out);
  and and_5 (and_5_out, and_3_out, nor_1_out, X_imm);
  and and_6 (and_6_out, and_3_out, nor_1_out, X_addr, t_ff_1_qn);
  and and_7 (and_7_out, and_3_out, nor_1_out, X_addr, t_ff_1_q);
  and and_8 (and_8_out, and_3_out, nor_2_out, Y_imm, t_ff_1_qn);
  and and_9 (and_9_out, and_3_out, nor_2_out, t_ff_1_q);
  Register #(.trigger("falling"), .width(32)) register_1 (
    .D(multiplexer_1_out), .en(write_temp), .clk(CLK_out), .Q(temp_reg));  // open: clr
  Register #(.width(32)) register_2 (
    .D(DATA_in), .en(write_IR), .clk(CLK_out), .Q({register_2_q, F, X, Y}));  // open: clr
  and and_10 (Y_imm, ~Y[0], Y[1], Y[2], Y[3], Y[4]);  // AND_Gate
  and and_11 (Y_addr, Y[0], Y[1], Y[2], Y[3], Y[4]);
  clock_edge_enabler clock_edge_enabler_2 (
    .CLK_in(CLK_out), .enable_falliong_edge(PC_write), .CLK_out(clock_edge_enabler_2_clk_out));  // open: enable_rising_edge
  nor nor_3 (nor_3_out, PC_write, increment_address);
  and and_12 (X_imm, ~X[0], X[1], X[2], X[3], X[4]);  // AND_Gate
  clock_edge_enabler clock_edge_enabler_3 (
    .CLK_in(CLK_out), .enable_rising_edge(pull_resistor_3_node), .enable_falliong_edge(enable_falling_edge),
    .CLK_out(clock_edge_enabler_3_clk_out));
  Pull_Resistor #(.pull(1)) pull_resistor_3 (.node(pull_resistor_3_node));
  and and_13 (X_addr, X[0], X[1], X[2], X[3], X[4]);
  not nor_4 (write_IR, and_7_out);  // NOR_Gate
  Counter #(.max('hffffffff), .width(32)) program_counter (
    .load(clock_edge_enabler_2_clk_out), .D(PC_in), .count(nor_3_out), .Q(PC_out),
    .clk(clock_edge_enabler_3_clk_out));  // open: carry, up, clr
  or or_1 (reg_write, and_5_out, and_7_out);
  nor nor_5 (both_regs, Y_imm, Y_addr, X_imm, X_addr);
  buf or_2 (write, and_8_out);  // OR_Gate
  buf or_3 (increment_address, and_7_out);  // OR_Gate
  Multiplexer #(.width(32)) multiplexer_2 (.in0(PC_out), .in1(address_alt_out), .out(ADDRESS_out), .sel(alt_addr));
  or or_4 (enable_falling_edge, and_5_out, and_6_out, and_8_out);
  Pull_Resistor #(.pull(1)) pull_resistor_4 (.node(pull_resistor_4_node));
  Multiplexer #(.width(32)) multiplexer_3 (
    .in0(temp_reg), .in1(reg_data_out), .out(address_alt_out), .sel(alt_addr_sel));
  Multiplexer #(.width(32)) multiplexer_4 (.in0(reg_data_out), .in1(temp_reg), .out(DATA_out), .sel(data_out_sel));
  Multiplexer #(.width(5)) multiplexer_5 (.in0(Y), .in1(pull_resistor_4_node), .out(multiplexer_5_out), .sel(F));
  buf or_5 (alt_addr, and_7_out);  // OR_Gate
  buf or_6 (delay_rising, and_9_out);  // OR_Gate
  Pull_Resistor pull_resistor_5 (.node(pull_resistor_5_node));
  Pull_Resistor pull_resistor_6 (.node(PC_in));
  Pull_Resistor pull_resistor_7 (.node(pull_resistor_7_node));
  Pull_Resistor pull_resistor_8 (.node(pull_resistor_8_node));
  Pull_Resistor pull_resistor_9 (.node(pull_resistor_9_node));
  Pull_Resistor pull_resistor_10 (.node(pull_resistor_10_node));
  Pull_Resistor pull_resistor_11 (.node(pull_resistor_11_node));
  Pull_Resistor pull_resistor_12 (.node(pull_resistor_12_node));
  Pull_Resistor pull_resistor_13 (.node(pull_resistor_13_node));
  Pull_Resistor pull_resistor_14 (.node(pull_resistor_14_node));
  Pull_Resistor pull_resistor_15 (.node(pull_resistor_15_node));
  Pull_Resistor pull_resistor_16 (.node(pull_resistor_16_node));
  Pull_Resistor pull_resistor_17 (.node(pull_resistor_17_node));
  Pull_Resistor pull_resistor_18 (.node(pull_resistor_18_node));
  Pull_Resistor pull_resistor_19 (.node(pull_resistor_19_node));
  Pull_Resistor pull_resistor_20 (.node(pull_resistor_20_node));
  Pull_Resistor pull_resistor_21 (.node(pull_resistor_21_node));
  Pull_Resistor pull_resistor_22 (.node(pull_resistor_22_node));
  Pull_Resistor pull_resistor_23 (.node(pull_resistor_23_node));
  Pull_Resistor pull_resistor_24 (.node(pull_resistor_24_node));
  Pull_Resistor pull_resistor_25 (.node(pull_resistor_25_node));
  Pull_Resistor pull_resistor_26 (.node(pull_resistor_26_node));
  Pull_Resistor pull_resistor_27 (.node(pull_resistor_27_node));
  Pull_Resistor pull_resistor_28 (.node(pull_resistor_28_node));
  Pull_Resistor pull_resistor_29 (.node(pull_resistor_29_node));
  Pull_Resistor pull_resistor_30 (.node(pull_resistor_30_node));
  Pull_Resistor pull_resistor_31 (.node(pull_resistor_31_node));
  Pull_Resistor pull_resistor_32 (.node(pull_resistor_32_node));
  Pull_Resistor pull_resistor_33 (.node(pull_resistor_33_node));
  Pull_Resistor pull_resistor_34 (.node(pull_resistor_34_node));
  or or_7 (delay_falling, and_6_out, and_7_out, and_8_out);
  Demultiplexer #(.select(5), .tristate("true"), .width(32)) demultiplexer_1 (
    .out0(pull_resistor_34_node), .out1(pull_resistor_33_node), .out2(pull_resistor_32_node),
    .out3(pull_resistor_31_node), .out4(pull_resistor_30_node), .out5(pull_resistor_29_node),
    .out6(pull_resistor_28_node), .out7(pull_resistor_27_node), .out8(pull_resistor_26_node),
    .out9(pull_resistor_25_node), .out10(pull_resistor_24_node), .out11(pull_resistor_23_node),
    .out12(pull_resistor_22_node), .out13(pull_resistor_21_node), .out14(pull_resistor_20_node),
    .out15(pull_resistor_19_node), .out16(pull_resistor_18_node), .out17(pull_resistor_17_node),
    .out18(pull_resistor_16_node), .out19(pull_resistor_15_node), .out20(pull_resistor_14_node),
    .out21(pull_resistor_13_node), .out22(pull_resistor_12_node), .out23(pull_resistor_11_node),
    .out24(pull_resistor_10_node), .out25(pull_resistor_9_node), .out26(pull_resistor_8_node),
    .out27(pull_resistor_7_node), .out28(PC_in), .out29(pull_resistor_5_node), .out30(data_out_t),
    .out31(data_out_t), .in(reg_data_in), .sel(multiplexer_5_out));
  buf or_8 (write_temp, and_6_out);  // OR_Gate
  buf or_9 (select_temp_in, pull_resistor_66_node);  // OR_Gate
  Multiplexer #(.select(2), .width(32)) multiplexer_6 (
    .in0(reg_data_out), .in1(ALU_out), .in2(temp_reg), .in3(undriven), .out(reg_data_in), .sel(2'b00));
  buf or_10 (alt_addr_sel, and_4_out);  // OR_Gate
  buf or_11 (data_out_sel, pull_resistor_66_node);  // OR_Gate
  Pull_Resistor pull_resistor_35 (.node(data_out_t));
  Pull_Resistor pull_resistor_36 (.node(pull_resistor_36_node));
  Pull_Resistor pull_resistor_37 (.node(PC_write));
  Pull_Resistor pull_resistor_38 (.node(pull_resistor_38_node));
  Pull_Resistor pull_resistor_39 (.node(pull_resistor_39_node));
  Pull_Resistor pull_resistor_40 (.node(pull_resistor_40_node));
  Pull_Resistor pull_resistor_41 (.node(pull_resistor_41_node));
  Pull_Resistor pull_resistor_42 (.node(pull_resistor_42_node));
  Pull_Resistor pull_resistor_43 (.node(pull_resistor_43_node));
  Pull_Resistor pull_resistor_44 (.node(pull_resistor_44_node));
  Pull_Resistor pull_resistor_45 (.node(pull_resistor_45_node));
  Pull_Resistor pull_resistor_46 (.node(pull_resistor_46_node));
  Pull_Resistor pull_resistor_47 (.node(pull_resistor_47_node));
  Pull_Resistor pull_resistor_48 (.node(pull_resistor_48_node));
  Pull_Resistor pull_resistor_49 (.node(pull_resistor_49_node));
  Pull_Resistor pull_resistor_50 (.node(pull_resistor_50_node));
  Pull_Resistor pull_resistor_51 (.node(pull_resistor_51_node));
  Pull_Resistor pull_resistor_52 (.node(pull_resistor_52_node));
  Pull_Resistor pull_resistor_53 (.node(pull_resistor_53_node));
  Pull_Resistor pull_resistor_54 (.node(pull_resistor_54_node));
  Pull_Resistor pull_resistor_55 (.node(pull_resistor_55_node));
  Pull_Resistor pull_resistor_56 (.node(pull_resistor_56_node));
  Pull_Resistor pull_resistor_57 (.node(pull_resistor_57_node));
  Pull_Resistor pull_resistor_58 (.node(pull_resistor_58_node));
  Pull_Resistor pull_resistor_59 (.node(pull_resistor_59_node));
  Pull_Resistor pull_resistor_60 (.node(pull_resistor_60_node));
  Pull_Resistor pull_resistor_61 (.node(pull_resistor_61_node));
  Pull_Resistor pull_resistor_62 (.node(pull_resistor_62_node));
  Pull_Resistor pull_resistor_63 (.node(pull_resistor_63_node));
  Pull_Resistor pull_resistor_64 (.node(pull_resistor_64_node));
  Pull_Resistor pull_resistor_65 (.node(pull_resistor_65_node));
  Register #(.trigger("falling"), .width(32)) register_3 (
    .D(pull_resistor_34_node), .en(pull_resistor_65_node), .clk(CLK_out), .Q(register_3_q));  // open: clr
  Pull_Resistor pull_resistor_66 (.node(pull_resistor_66_node));
  Register #(.trigger("falling"), .width(32)) register_4 (
    .D(pull_resistor_33_node), .en(pull_resistor_64_node), .clk(CLK_out), .Q(register_4_q));  // open: clr
  Demultiplexer #(.select(5), .tristate("true")) demultiplexer_2 (
    .out0(pull_resistor_65_node), .out1(pull_resistor_64_node), .out2(pull_resistor_63_node),
    .out3(pull_resistor_62_node), .out4(pull_resistor_61_node), .out5(pull_resistor_60_node),
    .out6(pull_resistor_59_node), .out7(pull_resistor_58_node), .out8(pull_resistor_57_node),
    .out9(pull_resistor_56_node), .out10(pull_resistor_55_node), .out11(pull_resistor_54_node),
    .out12(pull_resistor_53_node), .out13(pull_resistor_52_node), .out14(pull_resistor_51_node),
    .out15(pull_resistor_50_node), .out16(pull_resistor_49_node), .out17(pull_resistor_48_node),
    .out18(pull_resistor_47_node), .out19(pull_resistor_46_node), .out20(pull_resistor_45_node),
    .out21(pull_resistor_44_node), .out22(pull_resistor_43_node), .out23(pull_resistor_42_node),
    .out24(pull_resistor_41_node), .out25(pull_resistor_40_node), .out26(pull_resistor_39_node),
    .out27(pull_resistor_38_node), .out28(PC_write), .out29(pull_resistor_36_node),
    .out30(demultiplexer_2_out30), .out31(demultiplexer_2_out30), .in(reg_write), .sel(multiplexer_5_out));
  Register #(.trigger("falling"), .width(32)) register_5 (
    .D(pull_resistor_32_node), .en(pull_resistor_63_node), .clk(CLK_out), .Q(register_5_q));  // open: clr
  Multiplexer #(.select(5), .width(32)) multiplexer_7 (
    .in0(register_3_q), .in1(register_4_q), .in2(register_5_q), .in3(register_6_q), .in4(register_7_q),
    .in5(register_8_q), .in6(register_9_q), .in7(register_10_q), .in8(register_11_q), .in9(register_12_q),
    .in10(register_13_q), .in11(register_14_q), .in12(register_15_q), .in13(register_16_q),
    .in14(register_17_q), .in15(register_18_q), .in16(register_19_q), .in17(register_20_q),
    .in18(register_21_q), .in19(register_22_q), .in20(register_23_q), .in21(register_24_q),
    .in22(register_25_q), .in23(register_26_q), .in24(register_27_q), .in25(register_28_q),
    .in26(register_29_q), .in27(register_30_q), .in28(PC_out), .in29(register_31_q), .in30(DATA_in),
    .in31(DATA_in), .out(reg_data_out), .sel(X));
  Multiplexer #(.select(5), .width(32)) multiplexer_8 (
    .in0(register_3_q), .in1(register_4_q), .in2(register_5_q), .in3(register_6_q), .in4(register_7_q),
    .in5(register_8_q), .in6(register_9_q), .in7(register_10_q), .in8(register_11_q), .in9(register_12_q),
    .in10(register_13_q), .in11(register_14_q), .in12(register_15_q), .in13(register_16_q),
    .in14(register_17_q), .in15(register_18_q), .in16(register_19_q), .in17(register_20_q),
    .in18(register_21_q), .in19(register_22_q), .in20(register_23_q), .in21(register_24_q),
    .in22(register_25_q), .in23(register_26_q), .in24(register_27_q), .in25(register_28_q),
    .in26(register_29_q), .in27(register_30_q), .in28(PC_out), .in29(register_31_q), .in30(DATA_in),
    .in31(DATA_in), .out(reg_data_out_2), .sel(undriven_2));
  Pull_Resistor pull_resistor_67 (.node(demultiplexer_2_out30));
  Register #(.trigger("falling"), .width(32)) register_6 (
    .D(pull_resistor_31_node), .en(pull_resistor_62_node), .clk(CLK_out), .Q(register_6_q));  // open: clr
  Register #(.trigger("falling"), .width(32)) register_7 (
    .D(pull_resistor_30_node), .en(pull_resistor_61_node), .clk(CLK_out), .Q(register_7_q));  // open: clr
  Register #(.trigger("falling"), .width(32)) register_8 (
    .D(pull_resistor_29_node), .en(pull_resistor_60_node), .clk(CLK_out), .Q(register_8_q));  // open: clr
  Register #(.trigger("falling"), .width(32)) register_9 (
    .D(pull_resistor_28_node), .en(pull_resistor_59_node), .clk(CLK_out), .Q(register_9_q));  // open: clr
  Register #(.trigger("falling"), .width(32)) register_10 (
    .D(pull_resistor_27_node), .en(pull_resistor_58_node), .clk(CLK_out), .Q(register_10_q));  // open: clr
  Register #(.trigger("falling"), .width(32)) register_11 (
    .D(pull_resistor_26_node), .en(pull_resistor_57_node), .clk(CLK_out), .Q(register_11_q));  // open: clr
  Register #(.trigger("falling"), .width(32)) register_12 (
    .D(pull_resistor_25_node), .en(pull_resistor_56_node), .clk(CLK_out), .Q(register_12_q));  // open: clr
  Register #(.trigger("falling"), .width(32)) register_13 (
    .D(pull_resistor_24_node), .en(pull_resistor_55_node), .clk(CLK_out), .Q(register_13_q));  // open: clr
  Register #(.trigger("falling"), .width(32)) register_14 (
    .D(pull_resistor_23_node), .en(pull_resistor_54_node), .clk(CLK_out), .Q(register_14_q));  // open: clr
  Register #(.trigger("falling"), .width(32)) register_15 (
    .D(pull_resistor_22_node), .en(pull_resistor_53_node), .clk(CLK_out), .Q(register_15_q));  // open: clr
  Register #(.trigger("falling"), .width(32)) register_16 (
    .D(pull_resistor_21_node), .en(pull_resistor_52_node), .clk(CLK_out), .Q(register_16_q));  // open: clr
  Register #(.trigger("falling"), .width(32)) register_17 (
    .D(pull_resistor_20_node), .en(pull_resistor_51_node), .clk(CLK_out), .Q(register_17_q));  // open: clr
  Register #(.trigger("falling"), .width(32)) register_18 (
    .D(pull_resistor_19_node), .en(pull_resistor_50_node), .clk(CLK_out), .Q(register_18_q));  // open: clr
  Register #(.trigger("falling"), .width(32)) register_19 (
    .D(pull_resistor_18_node), .en(pull_resistor_49_node), .clk(CLK_out), .Q(register_19_q));  // open: clr
  Register #(.trigger("falling"), .width(32)) register_20 (
    .D(pull_resistor_17_node), .en(pull_resistor_48_node), .clk(CLK_out), .Q(register_20_q));  // open: clr
  Register #(.trigger("falling"), .width(32)) register_21 (
    .D(pull_resistor_16_node), .en(pull_resistor_47_node), .clk(CLK_out), .Q(register_21_q));  // open: clr
  Register #(.trigger("falling"), .width(32)) register_22 (
    .D(pull_resistor_15_node), .en(pull_resistor_46_node), .clk(CLK_out), .Q(register_22_q));  // open: clr
  Register #(.trigger("falling"), .width(32)) register_23 (
    .D(pull_resistor_14_node), .en(pull_resistor_45_node), .clk(CLK_out), .Q(register_23_q));  // open: clr
  Register #(.trigger("falling"), .width(32)) register_24 (
    .D(pull_resistor_13_node), .en(pull_resistor_44_node), .clk(CLK_out), .Q(register_24_q));  // open: clr
  Register #(.trigger("falling"), .width(32)) register_25 (
    .D(pull_resistor_12_node), .en(pull_resistor_43_node), .clk(CLK_out), .Q(register_25_q));  // open: clr
  Register #(.trigger("falling"), .width(32)) register_26 (
    .D(pull_resistor_11_node), .en(pull_resistor_42_node), .clk(CLK_out), .Q(register_26_q));  // open: clr
  Register #(.trigger("falling"), .width(32)) register_27 (
    .D(pull_resistor_10_node), .en(pull_resistor_41_node), .clk(CLK_out), .Q(register_27_q));  // open: clr
  Register #(.trigger("falling"), .width(32)) register_28 (
    .D(pull_resistor_9_node), .en(pull_resistor_40_node), .clk(CLK_out), .Q(register_28_q));  // open: clr
  Register #(.trigger("falling"), .width(32)) register_29 (
    .D(pull_resistor_8_node), .en(pull_resistor_39_node), .clk(CLK_out), .Q(register_29_q));  // open: clr
  Register #(.trigger("falling"), .width(32)) register_30 (
    .D(pull_resistor_7_node), .en(pull_resistor_38_node), .clk(CLK_out), .Q(register_30_q));  // open: clr
  Register #(.width(32)) register_31 (
    .D(pull_resistor_5_node), .en(pull_resistor_36_node), .clk(CLK_out), .Q(register_31_q));  // open: clr

  // Other names for the same wires on the sheet: CLK = CLK_out; immediate_data[31:0] = DATA_in; write_out = write

  // Notes on the sheet:
  //   load immediate
  //   load from address
  //   store immediate
  //   Register File
endmodule

module DOUBLE_CLOCK (
  input  in_1,
  output out_2
);

  wire not_1_out;

  not not_1 (not_1_out, in_1);
  xnor xnor_1 (out_2, not_1_out, in_1);
endmodule

module clock_edge_enabler (
  input  CLK_in,
  input  enable_rising_edge,
  input  enable_falliong_edge,
  output CLK_out
);

  wire and_1_out, nor_1_out, not_1_out;

  Pull_Resistor pull_resistor_1 (.node(CLK_in));
  Pull_Resistor #(.pull(1)) pull_resistor_2 (.node(enable_rising_edge));
  Pull_Resistor #(.pull(1)) pull_resistor_3 (.node(enable_falliong_edge));
  not not_1 (not_1_out, CLK_in);
  and and_1 (and_1_out, not_1_out, CLK_in, enable_rising_edge);
  nor nor_1 (nor_1_out, not_1_out, CLK_in, ~enable_falliong_edge);  // NOR_Gate
  Pull_Resistor pull_resistor_4 (.node(CLK_out));
  or or_1 (CLK_out, and_1_out, nor_1_out);
endmodule
